# Fritzing sketch Glowey (saved by Fritzing 1.0.6)
breadboards: 1

parts:
  Part1 = Arduino Nano (Rev3.0)
  LED1 = smd LED [color="White (4500K)" package="0603 [SMD]"]
  LED2 = smd LED [color="White (4500K)" package="0603 [SMD]"]
  LED3 = smd LED [color="White (4500K)" package="0603 [SMD]"]
  LED4 = smd LED [color="White (4500K)" package="0603 [SMD]"]
  HC-SR04_Sensor_1 = HC-SR04 Ultrasonic Distance Sensor
  M1 = fc-51 [package=THT]
  R1 = Resistor [tolerance=±5% resistance=220 package="0805 [SMD]"]
  R2 = Resistor [tolerance=±5% resistance=220 package="0805 [SMD]"]
  R3 = Resistor [tolerance=±5% resistance=220 package="0805 [SMD]"]
  R4 = Resistor [tolerance=±5% resistance=220 package="0805 [SMD]"]

nets:
  GND: Part1.GND, LED1.cathode, LED2.cathode, LED3.cathode, LED4.cathode, HC-SR04_Sensor_1.GND, M1.pin2
  N1: Part1.D2, M1.pin1
  N2: Part1.D3, HC-SR04_Sensor_1.ECHO
  N3: Part1.D4, HC-SR04_Sensor_1.TRIG
  N4: Part1.D5, R1.Pin_1
  N5: Part1.D6, R2.Pin_1
  N6: Part1.D7, R3.Pin_1
  N7: Part1.D8, R4.Pin_1
  VIN: Part1.VIN, HC-SR04_Sensor_1.VCC, M1.pin3
  N8: LED1.anode, R1.Pin_0
  N9: LED2.anode, R2.Pin_0
  N10: LED3.anode, R3.Pin_0
  N11: LED4.anode, R4.Pin_0

// code stored in the sketch: Glowey.ino

